// Digital circuit 4bits.dig as structural Verilog
module _4bits (
  input  in_1,
  input  in_2,
  input  in_3,
  input  in_4,
  input  in_5,
  input  in_6,
  input  in_7,
  input  in_8,
  output out_9,
  output out_10,
  output out_11,
  output out_12
);

  wire somador_1_out, somador_2_out, somador_3_out, somador_4_out;

  Seven_Seg_Hex seven_seg_hex_1 (.d({in_1, in_2, in_3, in_4}), .dp(1'b0));
  Seven_Seg_Hex seven_seg_hex_2 (.d({in_5, in_6, in_7, in_8}), .dp(1'b0));
  Somador somador_1 (.A(in_4), .B(in_8), .In(1'b0), .D(out_9), .Out(somador_1_out));
  Somador somador_2 (.A(in_3), .B(in_7), .In(somador_1_out), .D(out_10), .Out(somador_2_out));
  Somador somador_3 (.A(in_2), .B(in_6), .In(somador_2_out), .D(out_11), .Out(somador_3_out));
  Somador somador_4 (.A(in_1), .B(in_5), .In(somador_3_out), .D(out_12), .Out(somador_4_out));
  LED led_1 (.in(somador_4_out));
  Seven_Seg_Hex seven_seg_hex_3 (.d({out_12, out_11, out_10, out_9}), .dp(1'b0));

  // Notes on the sheet:
  //   Primeiro número
  //   Segundo número
endmodule
